// Logisim project ALU4.circ as structural Verilog: 1 circuit, main circuit ALU4
module ALU4 (
  input  [3:0] d1,
  input  [3:0] d2,
  input  [3:0] ctrl,
  output [3:0] outp
);

  wire [3:0] adder_1_out, and_1_out, bit_extender_2_out, bit_extender_3_out, nor_1_out, or_1_out, xor_1_out;
  wire [7:0] bit_extender_1_out, shifter_1_out, shifter_2_out;

  assign xor_1_out = d2 ^ {4{ctrl[0]}};  // XOR_Gate xor_1, 4 bits wide
  assign bit_extender_1_out = {{4{1'b0}}, d1};  // Bit_Extender bit_extender_1
  Adder #(.width(4)) adder_1 (.a(d1), .b(xor_1_out), .out(adder_1_out), .cin(ctrl[0]));  // open: cout
  Shifter shifter_1 (.in(bit_extender_1_out), .\dist (d2[2:0]), .out(shifter_1_out));
  Shifter #(.shift("lr")) shifter_2 (.in(bit_extender_1_out), .\dist (d2[2:0]), .out(shifter_2_out));
  assign and_1_out = d1 & d2;  // AND_Gate and_1, 4 bits wide
  assign or_1_out = d1 | d2;  // OR_Gate or_1, 4 bits wide
  assign nor_1_out = ~(d1 | d2);  // NOR_Gate nor_1, 4 bits wide
  Bit_Extender #(.out_width(4)) bit_extender_2 (.in(shifter_1_out), .out(bit_extender_2_out));
  Bit_Extender #(.out_width(4)) bit_extender_3 (.in(shifter_2_out), .out(bit_extender_3_out));
  Multiplexer #(.select(3), .width(4), .enable("false")) multiplexer_1 (
    .in0(adder_1_out), .in1(adder_1_out), .in2(bit_extender_2_out), .in3(bit_extender_3_out),
    .in4(and_1_out), .in5(or_1_out), .in6(nor_1_out), .out(outp), .sel(ctrl[2:0]));  // open: in7
endmodule
