// Logisim project BRNC.circ as structural Verilog: 1 circuit, main circuit BRNC
module BRNC (
  input  [3:0] r1,
  input  [3:0] r2,
  input  [7:0] pc_1,
  input  [7:0] ofst,
  input  bne,
  input  beq,
  output br,
  output [7:0] trgt
);

  wire and_1_out, and_2_out, and_3_out, not_1_out;
  wire [3:0] xnor_1_out;

  assign xnor_1_out = ~(r1 ^ r2);  // XNOR_Gate xnor_1, 4 bits wide
  Adder adder_1 (.a(pc_1), .b(ofst), .out(trgt), .cin(1'b0));  // open: cout
  and and_1 (and_1_out, xnor_1_out[0], xnor_1_out[1], xnor_1_out[2], xnor_1_out[3]);
  not not_1 (not_1_out, and_1_out);
  and and_2 (and_2_out, and_1_out, beq);
  and and_3 (and_3_out, not_1_out, bne);
  or or_1 (br, and_2_out, and_3_out);
endmodule
