// Logisim project CTRL.circ as structural Verilog: 1 circuit, main circuit CTRL
module CTRL (
  input  [3:0] opcode,
  output mw,
  output mr,
  output rw,
  output rd,
  output m2g,
  output asrc,
  output beq,
  output bneq,
  output j,
  output a2,
  output a1,
  output a0
);

  ROM #(.addrWidth(4), .dataWidth(12)) rom_1 (
    .addr(opcode), .data({mw, mr, rw, rd, m2g, asrc, beq, bneq, j, a2, a1, a0}));  // open: sel

  // Notes on the sheet:
  //   contents of rom_1 (hex, n*v repeats v):
  //   345 342 343 10 206 204 205 344 8 20 341 340 201 200 9c0 7c0
endmodule
