// Logisim project EX.circ as structural Verilog: 1 circuit, main circuit EX
module EX (
  input  [3:0] rsd,
  input  [3:0] rtd,
  input  [3:0] imdt,
  input  asrc,
  input  [2:0] ctrl,
  output [3:0] outp
);

  wire [3:0] multiplexer_1_out;

  Multiplexer #(.width(4), .enable("false")) multiplexer_1 (.in0(rtd), .in1(imdt), .out(multiplexer_1_out), .sel(asrc));
  ALU4 alu4_1 (.d1(rsd), .d2(multiplexer_1_out), .ctrl(ctrl), .outp(outp));
endmodule
