// Logisim project FWD.circ as structural Verilog: 1 circuit, main circuit FWD
module FWD (
  input  rw1,
  input  rw2,
  input  [3:0] rs,
  input  [3:0] rd1,
  input  [3:0] rd2,
  input  [3:0] rt,
  output [1:0] a,
  output [1:0] b
);

  wire and_2_out, and_4_out, not_1_out, not_2_out;
  wire [3:0] xnor_1_out, xnor_2_out, xnor_3_out, xnor_4_out;

  assign xnor_1_out = ~(rs ^ rd1);  // XNOR_Gate xnor_1, 4 bits wide
  assign xnor_2_out = ~(rs ^ rd2);  // XNOR_Gate xnor_2, 4 bits wide
  assign xnor_3_out = ~(rt ^ rd1);  // XNOR_Gate xnor_3, 4 bits wide
  assign xnor_4_out = ~(rt ^ rd2);  // XNOR_Gate xnor_4, 4 bits wide
  and and_1 (a[1], xnor_1_out[0], xnor_1_out[1], xnor_1_out[2], xnor_1_out[3], rw1);
  and and_2 (and_2_out, xnor_2_out[0], xnor_2_out[1], xnor_2_out[2], xnor_2_out[3], rw2);
  and and_3 (b[1], xnor_3_out[0], xnor_3_out[1], xnor_3_out[2], xnor_3_out[3], rw1);
  and and_4 (and_4_out, xnor_4_out[0], xnor_4_out[1], xnor_4_out[2], xnor_4_out[3], rw2);
  not not_1 (not_1_out, a[1]);
  not not_2 (not_2_out, b[1]);
  and and_5 (b[0], not_2_out, and_4_out);
  and and_6 (a[0], not_1_out, and_2_out);
endmodule
