// Logisim project ID.circ as structural Verilog: 1 circuit, main circuit ID
module ID (
  input  [3:0] r1,
  input  [3:0] r2,
  input  [3:0] wd,
  input  [3:0] rd,
  input  regWrite,
  input  clk,
  output [19:0] out_7,
  output [3:0] d1,
  output [3:0] d2
);

  wire and_1_out, and_2_out, and_3_out, and_4_out, and_5_out, and_6_out, decoder_1_out1, decoder_1_out2,
       decoder_1_out3, decoder_1_out4, decoder_1_out5, decoder_1_out6, rfwd_1_a, rfwd_1_b;
  wire [3:0] multiplexer_1_out, multiplexer_2_out, sp_q, zero_q;

  Decoder #(.select(3)) decoder_1 (
    .out1(decoder_1_out1), .out2(decoder_1_out2), .out3(decoder_1_out3), .out4(decoder_1_out4),
    .out5(decoder_1_out5), .out6(decoder_1_out6), .sel(rd[2:0]), .en(1'b1));  // open: out0, out7
  and and_1 (and_1_out, regWrite, decoder_1_out1);
  and and_2 (and_2_out, regWrite, decoder_1_out2);
  and and_3 (and_3_out, regWrite, decoder_1_out3);
  and and_4 (and_4_out, regWrite, decoder_1_out4);
  and and_5 (and_5_out, regWrite, decoder_1_out5);
  and and_6 (and_6_out, decoder_1_out6, regWrite);
  RFWD rfwd_1 (.rs(r1), .rt(r2), .dest(rd), .rw(regWrite), .a(rfwd_1_a), .b(rfwd_1_b));
  Register #(.width(4)) zero (.D(wd), .en(1'b0), .Q(zero_q), .clk(clk));  // open: clr
  Register #(.width(4)) register_1 (.D(wd), .en(and_1_out), .Q(out_7[19:16]), .clk(clk));  // open: clr
  Register #(.width(4)) register_2 (.D(wd), .en(and_2_out), .Q(out_7[15:12]), .clk(clk));  // open: clr
  Register #(.width(4)) register_3 (.D(wd), .en(and_3_out), .Q(out_7[11:8]), .clk(clk));  // open: clr
  Register #(.width(4)) register_4 (.D(wd), .en(and_4_out), .Q(out_7[7:4]), .clk(clk));  // open: clr
  Register #(.width(4)) register_5 (.D(wd), .en(and_5_out), .Q(out_7[3:0]), .clk(clk));  // open: clr
  Register #(.width(4)) sp (.D(wd), .en(and_6_out), .Q(sp_q), .clk(clk));  // open: clr
  Multiplexer #(.select(3), .width(4), .enable("false")) multiplexer_1 (
    .in0(zero_q), .in1(out_7[19:16]), .in2(out_7[15:12]), .in3(out_7[11:8]), .in4(out_7[7:4]),
    .in5(out_7[3:0]), .in6(sp_q), .out(multiplexer_1_out), .sel(r1[2:0]));  // open: in7
  Multiplexer #(.select(3), .width(4), .enable("false")) multiplexer_2 (
    .in0(zero_q), .in1(out_7[19:16]), .in2(out_7[15:12]), .in3(out_7[11:8]), .in4(out_7[7:4]),
    .in5(out_7[3:0]), .in6(sp_q), .out(multiplexer_2_out), .sel(r2[2:0]));  // open: in7
  Multiplexer #(.width(4), .enable("false")) multiplexer_3 (
    .in0(multiplexer_2_out), .in1(wd), .out(d2), .sel(rfwd_1_b));
  Multiplexer #(.width(4), .enable("false")) multiplexer_4 (
    .in0(multiplexer_1_out), .in1(wd), .out(d1), .sel(rfwd_1_a));
endmodule
