// Logisim project MEM.circ as structural Verilog: 1 circuit, main circuit MEM
module MEM (
  input  [3:0] wd,
  input  [7:0] addr,
  input  mw,
  input  clk,
  input  mr,
  output [3:0] data
);

  wire and_1_out, not_1_out, or_1_out;

  or or_1 (or_1_out, mw, and_1_out);
  RAM #(.dataWidth(4)) ram_1 (.addr(addr), .data(data), .sel(or_1_out), .clk(clk), .ld(and_1_out), .clr(1'b0));
  assign data = mw ? wd : 4'bz;  // Controlled_Buffer controlled_buffer_1
  and and_1 (and_1_out, not_1_out, 1'b1);
  not not_1 (not_1_out, mw);
endmodule
