// Logisim project PPM.circ as structural Verilog: 1 circuit, main circuit main
module main (
  output [3:0] out_1
);

  wire and_1_out, brnc_1_br, clock_1_out, ctrl_1_beq, ctrl_1_bneq, ctrl_1_j, ex_mem_1_c2_2, ex_mem_1_mr,
       ex_mem_1_mw, ex_mem_1_rw, id_ex_1_asrc, id_ex_1_mem2reg, id_ex_1_nop, id_ex_1_rd, mem_wb_1_mem2reg_2,
       mem_wb_1_rw_2, not_1_out, not_2_out, not_3_out, or_1_out, or_2_out, stall_1_stall;
  wire [1:0] fwd_1_a, fwd_1_b;
  wire [2:0] ctrl_1_a0, ctrl_1_asrc, ctrl_1_rw, id_ex_1_aop_2, id_ex_1_c1_2;
  wire [3:0] ex_1_outp, ex_mem_1_alu_2, ex_mem_1_rd_2, ex_mem_1_rso, ex_mem_1_wd_2, id_1_d1, id_1_d2,
       id_ex_1_imdt_2, id_ex_1_rd_imdt_2, id_ex_1_rs_2, id_ex_1_rsd_2, id_ex_1_rt_2, id_ex_1_rtd_2, if_1_op,
       if_1_r1, if_1_r2, if_1_r3_im, if_id_1_r1_2, if_id_1_r2_2, if_id_1_r3_im_2, mem_1_data, mem_wb_1_alu_2,
       mem_wb_1_memd_2, mem_wb_1_rd_2, multiplexer_1_out, multiplexer_2_out, multiplexer_3_out,
       multiplexer_4_out;
  wire [7:0] bit_extender_1_out, bit_extender_2_out, brnc_1_trgt, if_1_jump_2, if_1_pc_1, if_id_1_jump_2,
       if_id_1_pc_1_2;
  wire [19:0] id_1_out_7;

  IF if_1 (
    .i1(brnc_1_trgt), .jump(if_id_1_jump_2), .jump_2(if_1_jump_2), .s1(ctrl_1_j), .s0(brnc_1_br),
    .en(not_1_out), .clk(clock_1_out), .PC_1(if_1_pc_1), .r3_im(if_1_r3_im), .r2(if_1_r2), .r1(if_1_r1),
    .op(if_1_op));
  not not_1 (not_1_out, stall_1_stall);
  Clock clock_1 (.out(clock_1_out));
  or or_1 (or_1_out, brnc_1_br, ctrl_1_j);
  IF_ID if_id_1 (
    .pc_1(if_1_pc_1), .r3_im(if_1_r3_im), .r2(if_1_r2), .r1(if_1_r1), .op(if_1_op), .pc_1_2(if_id_1_pc_1_2),
    .r3_im_2(if_id_1_r3_im_2), .r2_2(if_id_1_r2_2), .r1_2(if_id_1_r1_2), .op_2(out_1), .clk(clock_1_out),
    .en(not_1_out), .jump(if_1_jump_2), .jump_2(if_id_1_jump_2), .flush(or_1_out));
  CTRL ctrl_1 (
    .opcode(out_1), .mw(ctrl_1_rw[2]), .mr(ctrl_1_rw[1]), .rw(ctrl_1_rw[0]), .rd(ctrl_1_asrc[2]),
    .m2g(ctrl_1_asrc[1]), .asrc(ctrl_1_asrc[0]), .beq(ctrl_1_beq), .bneq(ctrl_1_bneq), .j(ctrl_1_j),
    .a2(ctrl_1_a0[2]), .a1(ctrl_1_a0[1]), .a0(ctrl_1_a0[0]));
  BRNC brnc_1 (
    .r1(multiplexer_1_out), .r2(multiplexer_2_out), .pc_1(if_id_1_pc_1_2), .ofst(bit_extender_1_out),
    .bne(ctrl_1_bneq), .beq(ctrl_1_beq), .br(brnc_1_br), .trgt(brnc_1_trgt));
  ID id_1 (
    .r1(if_id_1_r1_2), .r2(if_id_1_r2_2), .wd(multiplexer_4_out), .rd(mem_wb_1_rd_2), .out_7(id_1_out_7),
    .regWrite(mem_wb_1_rw_2), .clk(clock_1_out), .d1(id_1_d1), .d2(id_1_d2));
  assign bit_extender_1_out = {{4{if_id_1_r3_im_2[3]}}, if_id_1_r3_im_2};  // Bit_Extender bit_extender_1
  STALL stall_1 (
    .rdest(multiplexer_3_out), .rs(if_id_1_r1_2), .rt(if_id_1_r2_2), .mr(id_ex_1_c1_2[1]), .br(or_2_out),
    .rw(id_ex_1_c1_2[0]), .nop(id_ex_1_nop), .stall(stall_1_stall), .memr(ex_mem_1_mr), .mmd(ex_mem_1_rd_2));
  ID_EX id_ex_1 (
    .clk(clock_1_out), .rsd(id_1_d1), .rtd(id_1_d2), .imdt(if_id_1_r3_im_2), .c1(ctrl_1_rw),
    .c2(ctrl_1_asrc), .aop(ctrl_1_a0), .aop_2(id_ex_1_aop_2), .c1_2(id_ex_1_c1_2), .imdt_2(id_ex_1_imdt_2),
    .rtd_2(id_ex_1_rtd_2), .rsd_2(id_ex_1_rsd_2), .rs(if_id_1_r1_2), .rt(if_id_1_r2_2),
    .rd_imdt(if_id_1_r3_im_2), .rs_2(id_ex_1_rs_2), .rt_2(id_ex_1_rt_2), .rd_imdt_2(id_ex_1_rd_imdt_2),
    .asrc(id_ex_1_asrc), .mem2reg(id_ex_1_mem2reg), .rd(id_ex_1_rd), .stl(stall_1_stall), .nop(id_ex_1_nop));
  Multiplexer #(.select(2), .width(4), .enable("false")) multiplexer_1 (
    .in0(id_ex_1_rsd_2), .in1(multiplexer_4_out), .in2(ex_mem_1_alu_2), .out(multiplexer_1_out), .sel(fwd_1_a));  // open: in3
  Multiplexer #(.select(2), .width(4), .enable("false")) multiplexer_2 (
    .in0(id_ex_1_rtd_2), .in1(multiplexer_4_out), .in2(ex_mem_1_alu_2), .out(multiplexer_2_out), .sel(fwd_1_b));  // open: in3
  FWD fwd_1 (
    .rs(id_ex_1_rs_2), .rd1(ex_mem_1_rd_2), .rd2(mem_wb_1_rd_2), .rt(id_ex_1_rt_2), .rw1(ex_mem_1_rw),
    .rw2(mem_wb_1_rw_2), .a(fwd_1_a), .b(fwd_1_b));
  Hex_Digit_Display hex_digit_display_1 (.value(id_1_out_7[15:12]));  // open: dp
  Hex_Digit_Display hex_digit_display_2 (.value(id_1_out_7[19:16]));  // open: dp
  EX ex_1 (
    .rsd(multiplexer_1_out), .rtd(multiplexer_2_out), .imdt(id_ex_1_imdt_2), .asrc(id_ex_1_asrc),
    .ctrl(id_ex_1_aop_2), .outp(ex_1_outp));
  Multiplexer #(.width(4), .enable("false")) multiplexer_3 (
    .in0(id_ex_1_rd_imdt_2), .in1(id_ex_1_rt_2), .out(multiplexer_3_out), .sel(id_ex_1_rd));
  or or_2 (or_2_out, ctrl_1_beq, ctrl_1_bneq);
  Hex_Digit_Display hex_digit_display_3 (.value(id_1_out_7[11:8]));  // open: dp
  EX_MEM ex_mem_1 (
    .alu(ex_1_outp), .wd(multiplexer_2_out), .c1(id_ex_1_c1_2), .c2(id_ex_1_mem2reg), .alu_2(ex_mem_1_alu_2),
    .wd_2(ex_mem_1_wd_2), .c2_2(ex_mem_1_c2_2), .in_6(clock_1_out), .rd_2(ex_mem_1_rd_2),
    .rd(multiplexer_3_out), .rw(ex_mem_1_rw), .mr(ex_mem_1_mr), .mw(ex_mem_1_mw), .rso(ex_mem_1_rso),
    .rsi(id_ex_1_rs_2));
  Hex_Digit_Display hex_digit_display_4 (.value(id_1_out_7[7:4]));  // open: dp
  assign bit_extender_2_out = {{4{and_1_out}}, ex_mem_1_alu_2};  // Bit_Extender bit_extender_2
  MEM mem_1 (
    .wd(ex_mem_1_wd_2), .addr(bit_extender_2_out), .mw(ex_mem_1_mw), .clk(clock_1_out), .mr(ex_mem_1_mr),
    .data(mem_1_data));
  Hex_Digit_Display hex_digit_display_5 (.value(id_1_out_7[3:0]));  // open: dp
  not not_2 (not_2_out, ex_mem_1_rso[3]);
  MEM_WB mem_wb_1 (
    .alu(ex_mem_1_alu_2), .memd(mem_1_data), .rw(ex_mem_1_rw), .mem2reg(ex_mem_1_c2_2),
    .alu_2(mem_wb_1_alu_2), .memd_2(mem_wb_1_memd_2), .rw_2(mem_wb_1_rw_2), .mem2reg_2(mem_wb_1_mem2reg_2),
    .clk(clock_1_out), .rd_2(mem_wb_1_rd_2), .rd(ex_mem_1_rd_2));
  not not_3 (not_3_out, ex_mem_1_rso[0]);
  and and_1 (and_1_out, not_2_out, ex_mem_1_rso[2], ex_mem_1_rso[1], not_3_out);
  Multiplexer #(.width(4), .enable("false")) multiplexer_4 (
    .in0(mem_wb_1_alu_2), .in1(mem_wb_1_memd_2), .out(multiplexer_4_out), .sel(mem_wb_1_mem2reg_2));
endmodule
