// Logisim project RFWD.circ as structural Verilog: 1 circuit, main circuit RFWD
module RFWD (
  input  rw,
  input  [3:0] rs,
  input  [3:0] rt,
  input  [3:0] dest,
  output a,
  output b
);

  wire [3:0] xnor_1_out, xnor_2_out;

  assign xnor_1_out = ~(rs ^ dest);  // XNOR_Gate xnor_1, 4 bits wide
  assign xnor_2_out = ~(rt ^ dest);  // XNOR_Gate xnor_2, 4 bits wide
  and and_1 (a, xnor_1_out[0], xnor_1_out[1], xnor_1_out[2], xnor_1_out[3], rw);
  and and_2 (b, xnor_2_out[0], xnor_2_out[1], xnor_2_out[2], xnor_2_out[3], rw);
endmodule
