// Logisim project SCM.circ as structural Verilog: 1 circuit, main circuit SCM
module SCM (
);

  wire clock_1_out, ctrl_1_asrc, ctrl_1_beq, ctrl_1_bneq, ctrl_1_m2g, ctrl_1_mr, ctrl_1_mw, ctrl_1_rd,
       ctrl_1_rw, if_1_p2, if_1_p3;
  wire [2:0] ctrl_1_a0;
  wire [3:0] ex_1_outp, id_1_d1, id_1_d2, if_1_p6, if_1_p7, if_1_p8, if_1_p9, mem_1_data, multiplexer_1_out;
  wire [7:0] bit_extender_1_out, bit_extender_2_out, if_1_p1, if_1_p5;
  wire [19:0] id_1_out_9;

  Clock clock_1 (.out(clock_1_out));
  // IF if_1: pin names not known; wires that end beside it: if_1_p1, if_1_p2, if_1_p3, clock_1_out, if_1_p5, if_1_p6, if_1_p7, if_1_p8, if_1_p9
  assign bit_extender_1_out = {{4{if_1_p6[3]}}, if_1_p6};  // Bit_Extender bit_extender_1
  BRNC brnc_1 (
    .r1(id_1_d1), .r2(id_1_d2), .pc_1(if_1_p5), .ofst(bit_extender_1_out), .bne(ctrl_1_bneq),
    .beq(ctrl_1_beq), .br(if_1_p3), .trgt(if_1_p1));
  ID id_1 (
    .r1(if_1_p8), .r2(if_1_p7), .wd(multiplexer_1_out), .rd(if_1_p6), .rt(if_1_p7), .out_9(id_1_out_9),
    .wr(ctrl_1_rd), .regWrite(ctrl_1_rw), .clk(clock_1_out), .d1(id_1_d1), .d2(id_1_d2));
  CTRL ctrl_1 (
    .opcode(if_1_p9), .mw(ctrl_1_mw), .mr(ctrl_1_mr), .rw(ctrl_1_rw), .rd(ctrl_1_rd), .m2g(ctrl_1_m2g),
    .asrc(ctrl_1_asrc), .beq(ctrl_1_beq), .bneq(ctrl_1_bneq), .j(if_1_p2), .a2(ctrl_1_a0[2]),
    .a1(ctrl_1_a0[1]), .a0(ctrl_1_a0[0]));
  Hex_Digit_Display hex_digit_display_1 (.value(id_1_out_9[19:16]));  // open: dp
  Hex_Digit_Display hex_digit_display_2 (.value(id_1_out_9[15:12]));  // open: dp
  EX ex_1 (.rsd(id_1_d1), .rtd(id_1_d2), .imdt(if_1_p6), .asrc(ctrl_1_asrc), .ctrl(ctrl_1_a0), .outp(ex_1_outp));
  Hex_Digit_Display hex_digit_display_3 (.value(id_1_out_9[11:8]));  // open: dp
  assign bit_extender_2_out = {{4{1'b0}}, ex_1_outp};  // Bit_Extender bit_extender_2
  Hex_Digit_Display hex_digit_display_4 (.value(id_1_out_9[7:4]));  // open: dp
  MEM mem_1 (
    .wd(id_1_d2), .addr(bit_extender_2_out), .mw(ctrl_1_mw), .clk(clock_1_out), .mr(ctrl_1_mr),
    .data(mem_1_data));
  Hex_Digit_Display hex_digit_display_5 (.value(id_1_out_9[3:0]));  // open: dp
  Multiplexer #(.width(4), .enable("false")) multiplexer_1 (
    .in0(ex_1_outp), .in1(mem_1_data), .out(multiplexer_1_out), .sel(ctrl_1_m2g));
endmodule
