// Logisim project STALL.circ as structural Verilog: 1 circuit, main circuit STALL
module STALL (
  input  br,
  input  rw,
  input  nop,
  input  mr,
  input  [3:0] rdest,
  input  [3:0] rs,
  input  [3:0] rt,
  input  memr,
  input  [3:0] mmd,
  output stall
);

  wire and_1_out, and_2_out, and_3_out, and_4_out, and_5_out, and_6_out, and_7_out, or_1_out, or_2_out,
       or_3_out;
  wire [3:0] xnor_1_out, xnor_2_out, xnor_3_out, xnor_4_out;

  assign xnor_1_out = ~(rdest ^ rs);  // XNOR_Gate xnor_1, 4 bits wide
  assign xnor_2_out = ~(rt ^ rdest);  // XNOR_Gate xnor_2, 4 bits wide
  assign xnor_3_out = ~(mmd ^ rs);  // XNOR_Gate xnor_3, 4 bits wide
  assign xnor_4_out = ~(mmd ^ rt);  // XNOR_Gate xnor_4, 4 bits wide
  or or_1 (or_1_out, mr, and_5_out);
  and and_1 (and_1_out, xnor_1_out[0], xnor_1_out[1], xnor_1_out[2], xnor_1_out[3], or_1_out);
  and and_2 (and_2_out, xnor_2_out[0], xnor_2_out[1], xnor_2_out[2], xnor_2_out[3], or_1_out);
  and and_3 (and_3_out, xnor_3_out[0], xnor_3_out[1], xnor_3_out[2], xnor_3_out[3], and_7_out);
  and and_4 (and_4_out, xnor_4_out[0], xnor_4_out[1], xnor_4_out[2], xnor_4_out[3], and_7_out);
  and and_5 (and_5_out, br, rw);
  or or_2 (or_2_out, and_1_out, and_2_out);
  or or_3 (or_3_out, and_3_out, and_4_out);
  and and_6 (and_6_out, br, nop);
  or or_4 (stall, or_2_out, and_6_out, or_3_out);
  and and_7 (and_7_out, memr, br);
endmodule
