// Logisim project registers.circ as structural Verilog: 4 circuits, main circuit IF/ID
module IF_ID (
  input  [7:0] jump,
  input  flush,
  input  [7:0] pc_1,
  input  [3:0] r3_im,
  input  [3:0] r2,
  input  [3:0] r1,
  input  [3:0] op,
  input  en,
  input  clk,
  output [7:0] jump_2,
  output [7:0] pc_1_2,
  output [3:0] r3_im_2,
  output [3:0] r2_2,
  output [3:0] r1_2,
  output [3:0] op_2
);

  wire [23:0] multiplexer_1_out;

  Multiplexer #(.width(24), .enable("false")) multiplexer_1 (
    .in0({op, r1, r2, r3_im, pc_1}), .in1({24{1'b0}}), .out(multiplexer_1_out), .sel(flush));
  Register register_1 (.D(jump), .en(en), .Q(jump_2), .clk(clk));  // open: clr
  Register #(.width(24)) register_2 (
    .D(multiplexer_1_out), .en(en), .Q({op_2, r1_2, r2_2, r3_im_2, pc_1_2}), .clk(clk));  // open: clr
endmodule

module ID_EX (
  input  [3:0] rsd,
  input  [3:0] rtd,
  input  [3:0] imdt,
  input  [2:0] c1,
  input  [2:0] c2,
  input  [2:0] aop,
  input  [3:0] rs,
  input  [3:0] rt,
  input  [3:0] rd_imdt,
  input  clk,
  input  stl,
  output [3:0] rsd_2,
  output [3:0] rtd_2,
  output [3:0] imdt_2,
  output [2:0] c1_2,
  output asrc,
  output mem2reg,
  output [2:0] aop_2,
  output rd,
  output [3:0] rs_2,
  output [3:0] rt_2,
  output [3:0] rd_imdt_2,
  output nop
);

  wire [2:0] multiplexer_1_out, multiplexer_2_out;

  Multiplexer #(.width(3), .enable("false")) multiplexer_1 (.in0(c1), .in1(3'b000), .out(multiplexer_1_out), .sel(stl));
  Multiplexer #(.width(3), .enable("false")) multiplexer_2 (.in0(c2), .in1(3'b000), .out(multiplexer_2_out), .sel(stl));
  Register #(.width(21)) register_1 (
    .D({aop, multiplexer_2_out, multiplexer_1_out, imdt, rtd, rsd}), .en(1'b1),
    .Q({aop_2, rd, mem2reg, asrc, c1_2, imdt_2, rtd_2, rsd_2}), .clk(clk));  // open: clr
  Register #(.width(12)) register_2 (
    .D({rd_imdt, rt, rs}), .en(1'b1), .Q({rd_imdt_2, rt_2, rs_2}), .clk(clk));  // open: clr
  Comparator #(.width(12), .mode("unsigned")) comparator_1 (
    .a({rd_imdt_2, rt_2, rs_2}), .b({12{1'b0}}), .eq(nop));  // open: gt, lt
endmodule

module EX_MEM (
  input  [3:0] alu,
  input  [3:0] wd,
  input  [2:0] c1,
  input  c2,
  input  [3:0] rd,
  input  in_6,
  input  [3:0] rsi,
  output [3:0] rso,
  output [3:0] alu_2,
  output [3:0] wd_2,
  output rw,
  output mr,
  output mw,
  output c2_2,
  output [3:0] rd_2
);

  Register #(.width(12)) register_1 (
    .D({c2, c1, wd, alu}), .en(1'b1), .Q({c2_2, mw, mr, rw, wd_2, alu_2}), .clk(in_6));  // open: clr
  Register register_2 (.D({rd, rsi}), .en(1'b1), .Q({rd_2, rso}), .clk(in_6));  // open: clr
endmodule

module MEM_WB (
  input  [3:0] alu,
  input  [3:0] memd,
  input  rw,
  input  mem2reg,
  input  [3:0] rd,
  input  clk,
  output [3:0] alu_2,
  output [3:0] memd_2,
  output rw_2,
  output mem2reg_2,
  output [3:0] rd_2
);

  Register #(.width(10)) register_1 (
    .D({mem2reg, rw, memd, alu}), .en(1'b1), .Q({mem2reg_2, rw_2, memd_2, alu_2}), .clk(clk));  // open: clr
  Register #(.width(4)) register_2 (.D(rd), .en(1'b1), .Q(rd_2), .clk(clk));  // open: clr
endmodule
